# Fritzing sketch EnergyMeter (saved by Fritzing 0.9.1b)
circuit board: 5cm x 5cm
breadboards: 1

parts:
  R1 = Resistor [tolerance=±5% resistance=150k package=THT]
  BPW40 = LTR-301 [package=ltr-301]
  R2 = Resistor [tolerance=±5% resistance=270 package=THT]
  U1 = 555 Timer [package="DIP8 [THT]"]
  LED1 = LED - 5mm [color="Red (633nm)" package="5 mm [THT]"]
  J1 = female pin header, 3 pins [form="♀ (female)"]

nets:
  N1: R1.Pin_0, BPW40.C, U1.Trigger, U1.Threshold
  3.3V: R1.Pin_1, U1.Reset, U1.Vcc_Supply_Voltage, J1.pin1
  GND: BPW40.E, R2.Pin_0, U1.Ground, J1.pin3
  N2: R2.Pin_1, LED1.cathode
  N3: U1.Output, LED1.anode, J1.pin2

notes:
  EnergyMeter
